# Fritzing sketch SOTAbots sensors (saved by Fritzing 0.9.3b)
perfboards: 1

parts:
  Part1 = Arduino Mega 2560 (Rev3)
  Part4 = Humidity Temperature Sensor SHT15  # not connected
  Part5 = Humidity Temperature Sensor SHT15
  Part18 = Ambient Light Sensor (TEMT6000 Breakout Board)
  Part19 = Ambient Light Sensor (TEMT6000 Breakout Board)
  Part20 = Ambient Light Sensor (TEMT6000 Breakout Board)
  Part21 = Ambient Light Sensor (TEMT6000 Breakout Board)
  Part22 = Ambient Light Sensor (TEMT6000 Breakout Board)
  Part23 = Ambient Light Sensor (TEMT6000 Breakout Board)
  Part24 = Ambient Light Sensor (TEMT6000 Breakout Board)
  Part25 = Ambient Light Sensor (TEMT6000 Breakout Board)
  Part26 = Ambient Light Sensor (TEMT6000 Breakout Board)
  Part27 = Ambient Light Sensor (TEMT6000 Breakout Board)
  Part28 = Ambient Light Sensor (TEMT6000 Breakout Board)
  Part29 = Ambient Light Sensor (TEMT6000 Breakout Board)
  Part30 = Ambient Light Sensor (TEMT6000 Breakout Board)
  Part31 = Ambient Light Sensor (TEMT6000 Breakout Board)
  Part32 = Ambient Light Sensor (TEMT6000 Breakout Board)

nets:
  N1: Part1.A8, Part21.S
  N2: Part1.A9, Part20.S
  N3: Part1.A10, Part19.S
  N4: Part1.A11, Part18.S
  N5: Part1.A12, Part24.S
  N6: Part1.A13, Part29.S
  N7: Part1.A0, Part30.S
  N8: Part1.A1, Part28.S
  N9: Part1.A2, Part27.S
  N10: Part1.A3, Part26.S
  N11: Part1.A4, Part25.S
  N12: Part1.A5, Part23.S
  N13: Part1.A6, Part22.S
  N14: Part1.A7, Part32.S
  N15: Part1.SCL, Part5.SCL
  N16: Part1.SDA, Part5.SDA
  3V3: Part1.3V3, Part5.VCC
  5V: Part1.5V, Part31.VCC
  GND: Part1.GND, Part5.GND, Part29.GND, Part31.GND
